# Fritzing sketch Scheme (saved by Fritzing 0.9.4)

parts:
  Компонент1 = Arduino Nano (Rev3.0)
  Компонент3 = Bluetooth HC-06
  Компонент4 = Matrix LED de 8x8 basada en MAX7219  # not connected
  Power_plug1 = Power plug
  Компонент5 = Matrix LED de 8x8 basada en MAX7219  # not connected
  Компонент6 = Matrix LED de 8x8 basada en MAX7219  # not connected
  Компонент7 = Matrix LED de 8x8 basada en MAX7219

nets:
  GND: Компонент1.GND, Power_plug1.GND
  N1: Компонент1.D2, Компонент3.TXD
  N2: Компонент1.D3, Компонент3.RXD
  N3: Компонент1.D10, Компонент7.CS
  N4: Компонент1.D11/MOSI, Компонент7.DIN
  5V: Компонент1.5V, Power_plug1.VCC
  N5: Компонент1.D13/SCK, Компонент7.CLK
